# Fritzing sketch PEW PCB (saved by Fritzing 0.9.2b)
circuit board: 4.53822cm x 4.74793cm
breadboards: 1

parts:
  Switch = Toggle Switch [package=THT]
  SW3 = DIP SWITCH [package=dipswitch-02]
  SW4 = DIP SWITCH [package=dipswitch-02]
  Part1 = Adafruit Pro Trinket 5V 16MHz [part_number="Adafruit #2000"]
  Servo = Basic Servo
  I2C = screw terminal, 3 pins
  IR_Sensor = screw terminal, 3 pins
  -_Power_+ = screw terminal, 2 pins

nets:
  N1: Switch.L1, Part1.VBAT, IR_Sensor.pin1
  N2: Switch.COM, Servo.vcc, -_Power_+.pin2
  GND: SW3.1, SW3.2, SW4.1, SW4.2, Part1.GND, Servo.gnd, I2C.pin1, IR_Sensor.pin2, -_Power_+.pin1
  N3: SW3.3, Part1.A1
  N4: SW3.4, Part1.A0
  N5: SW4.3, Part1.A3
  N6: SW4.4, Part1.A2
  N7: Part1.D4, IR_Sensor.pin3
  N8: Part1.D9, Servo.pulse
  N9: Part1.A4, I2C.pin2
  N10: Part1.A5, I2C.pin3

notes:
  G  A4  A5
  +  -  D4
  Cybernath Labs
  PEW PCBv1
  off   on
  -  +  ~

custom parts:
  Adafruit Pro Trinket 5V 16MHz: Trinket's got a big sister in town - the Pro Trinket 5V! Pro Trinket combines everything you love about Trinket with the familiarity of the common core Arduino chip, the ATmega328. It's like an Arduino Pro Mini with more pins and USB tossed in, so delicious. Trinket's a year old now, and while its been great to see tons of tiny projects, sometimes you just need more pins, more FLASH, and more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
